// Logisim project 4-bit Subtractor.circ as structural Verilog: 1 circuit, main circuit main
module main (
  input  in_1,
  input  [3:0] in_2,
  input  [3:0] in_3,
  output [3:0] out_4,
  output out_5
);

  Subtractor #(.width(4)) subtractor_1 (.a(in_2), .b(in_3), .out(out_4), .bin(in_1), .bout(out_5));
endmodule
